# Fritzing sketch Project (saved by Fritzing 0.9.4)
circuit board: 8.46667cm x 5.64444cm
breadboards: 1

parts:
  U1 = ESP32-38PinWide [part_number=ESP32-38PinWide]
  Componente1 = SRF05 Ultrasonic Rangefinder
  Mod1 = KY-019 5V Relay Module [package="Breakout board"]
  Mini_Water_Pump_3-6VDC1 = Mini Water Pump 3-6VDC [part_number="Mini Water Pump 3-6VDC" chip_label=IC package="DIP (Dual Inline) [THT]"]
  Q1 = NPN-Transistor [package="TO92 [THT]"]
  R1 = Resistor [tolerance=±5% resistance=10k package="1206 [SMD]"]
  R2 = Resistor [tolerance=±5% resistance=10k package="1206 [SMD]"]
  Capacitive_Soil_Moisture_Sensor1 = DFRobot Capacitive Soil Moisture Sensor V1.0 [part_number=SEN0193]
  A1 = DHT22 module

nets:
  N1: U1.GPIO34, Componente1.Echo
  N2: U1.GPIO35, Componente1.Trig
  N3: U1.GPIO32, Capacitive_Soil_Moisture_Sensor1.A
  N4: U1.GPIO14, R1.Pin_0
  N5: U1.GPIO12, A1.Out
  GND: U1.GND, Componente1.GND, Mod1.Common, Q1.E, Capacitive_Soil_Moisture_Sensor1.GND, A1.-
  VCC: U1.VIN, Componente1.VCC, Mod1.+, Mini_Water_Pump_3-6VDC1.-M, R2.Pin_1, Capacitive_Soil_Moisture_Sensor1.VCC, A1.+
  N6: Mod1.S, Q1.C, R2.Pin_0
  N7: Mod1.NC, Mini_Water_Pump_3-6VDC1.+M
  N8: Q1.B, R1.Pin_1

custom parts:
  ESP32-38PinWide: Generic 38-Pin ESP32 with wide format (only access to one side of pins on a breadboard) based on Stephen Lilley's HiLetgo ESP-WROOM-32 ESP32 ESP-32S Development Board.
  KY-019 5V Relay Module: KY-019 5V Relay module, used to control AC circuits. (Special thanks to vanepp for fixing the PCB holes and other errors)
  DFRobot Capacitive Soil Moisture Sensor V1.0: DFRobot Capacitive Soil Moisture Sensor V1.0 This product measures soil moisture levels by capacitive sensing, rather than resistive sensing like other types of moisture sensor. It is made of a corrosion resistant material giving it a long service life. Insert it into soil and impress your friends with the real-time soil moisture data! The product includes an on-board voltage regulator which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
  DHT22 module: DHT22 module. Pins VCC Data GND.
